// Logisim project ALU_ALU.circ as structural Verilog: 4 circuits, main circuit ALU
module ALU (
  input  [3:0] ALUC,
  input  [15:0] A,
  input  [15:0] B,
  input  CYin,
  output [15:0] Z,
  output CYout
);

  wire and_1_out, and_2_out, and_4_out, and_5_out, and_7_out, and_8_out, and_9_out, and_12_out, and_13_out,
       CY, CYin_t, multiplexer_1_out, notALUC0, notALUC1, notALUC2, notALUC3;
  wire [0:0] and_11_out;
  wire [15:0] alu_full_adder_16_1_sum_out, and_6_out, or_1_out;

  not not_1 (notALUC0, ALUC[0]);
  not not_2 (notALUC1, ALUC[1]);
  not not_3 (notALUC2, ALUC[2]);
  not not_4 (notALUC3, ALUC[3]);
  and and_1 (and_1_out, notALUC0, ALUC[1], notALUC2, notALUC3);
  and and_2 (and_2_out, ALUC[0], ALUC[1], notALUC2, notALUC3);
  and and_3 (CYin_t, CYin, ALUC[0]);
  assign Z = and_1_out ? ~A : 16'bz;  // Controlled_Inverter controlled_inverter_1
  assign Z = and_2_out ? ~B : 16'bz;  // Controlled_Inverter controlled_inverter_2
  Multiplexer #(.enable("false")) multiplexer_1 (.in0(CY), .in1(1'b1), .out(multiplexer_1_out), .sel(ALUC[3]));
  and and_4 (and_4_out, notALUC0, notALUC1, notALUC2, notALUC3);
  and and_5 (and_5_out, ALUC[0], notALUC1, notALUC2, notALUC3);
  assign and_6_out = A & B;  // AND_Gate and_6, 16 bits wide
  and and_7 (and_7_out, ALUC[0], ALUC[1], ALUC[2], notALUC3);
  assign or_1_out = A | B;  // OR_Gate or_1, 16 bits wide
  and and_8 (and_8_out, notALUC0, ALUC[1], ALUC[2], notALUC3);
  ALU_full_adder_16 alu_full_adder_16_1 (
    .Ain(A), .Bin(B), .Carryin(CYin_t), .SUM_out(alu_full_adder_16_1_sum_out), .Carry_out(CY));
  assign Z = and_4_out ? A : 16'bz;  // Controlled_Buffer controlled_buffer_1
  assign Z = and_5_out ? B : 16'bz;  // Controlled_Buffer controlled_buffer_2
  assign Z = and_8_out ? or_1_out : 16'bz;  // Controlled_Buffer controlled_buffer_3
  and and_9 (and_9_out, notALUC1, ALUC[2], notALUC3);
  and and_10 (CYout, ALUC[2], multiplexer_1_out);
  assign Z = and_7_out ? and_6_out : 16'bz;  // Controlled_Buffer controlled_buffer_4
  assign Z = and_9_out ? alu_full_adder_16_1_sum_out : 16'bz;  // Controlled_Buffer controlled_buffer_5
  and and_11 (and_11_out[0], multiplexer_1_out, ALUC[0]);
  and and_12 (and_12_out, notALUC0, ALUC[1], notALUC2, ALUC[3]);
  assign Z = and_12_out ? ~{{15{1'b0}}, and_11_out[0]} : 16'bz;  // Controlled_Inverter controlled_inverter_3
  assign Z = and_13_out ? {{15{1'b0}}, and_11_out[0]} : 16'bz;  // Controlled_Buffer controlled_buffer_6
  and and_13 (and_13_out, notALUC1, notALUC2, ALUC[3]);

  // Other names for the same wires on the sheet: ALU_OUT[15:0] = Z
endmodule

module ALU_full_adder (
  input  Xin,
  input  Yin,
  input  Cin,
  output SUMout,
  output Cout
);

  wire and_1_out, and_2_out, xor_1_out;

  xor xor_1 (xor_1_out, Xin, Yin);
  and and_1 (and_1_out, xor_1_out, Cin);
  and and_2 (and_2_out, Yin, Xin);
  xor xor_2 (SUMout, xor_1_out, Cin);
  or or_1 (Cout, and_1_out, and_2_out);
endmodule

module ALU_full_adder_16 (
  input  [15:0] Ain,
  input  [15:0] Bin,
  input  Carryin,
  output [15:0] SUM_out,
  output Carry_out
);

  wire C0, C1, C2, C3, C4, C5, C6, C7, C8, C9, C10, C11, C12, C13, C14;

  ALU_full_adder alu_full_adder_1 (.Xin(Ain[0]), .Yin(Bin[0]), .Cin(Carryin), .SUMout(SUM_out[0]), .Cout(C0));
  ALU_full_adder alu_full_adder_2 (.Xin(Ain[1]), .Yin(Bin[1]), .Cin(C0), .SUMout(SUM_out[1]), .Cout(C1));
  ALU_full_adder alu_full_adder_3 (.Xin(Ain[2]), .Yin(Bin[2]), .Cin(C1), .SUMout(SUM_out[2]), .Cout(C2));
  ALU_full_adder alu_full_adder_4 (.Xin(Ain[3]), .Yin(Bin[3]), .Cin(C2), .SUMout(SUM_out[3]), .Cout(C3));
  ALU_full_adder alu_full_adder_5 (.Xin(Ain[4]), .Yin(Bin[4]), .Cin(C3), .SUMout(SUM_out[4]), .Cout(C4));
  ALU_full_adder alu_full_adder_6 (.Xin(Ain[5]), .Yin(Bin[5]), .Cin(C4), .SUMout(SUM_out[5]), .Cout(C5));
  ALU_full_adder alu_full_adder_7 (.Xin(Ain[6]), .Yin(Bin[6]), .Cin(C5), .SUMout(SUM_out[6]), .Cout(C6));
  ALU_full_adder alu_full_adder_8 (.Xin(Ain[7]), .Yin(Bin[7]), .Cin(C6), .SUMout(SUM_out[7]), .Cout(C7));
  ALU_full_adder alu_full_adder_9 (.Xin(Ain[8]), .Yin(Bin[8]), .Cin(C7), .SUMout(SUM_out[8]), .Cout(C8));
  ALU_full_adder alu_full_adder_10 (.Xin(Ain[9]), .Yin(Bin[9]), .Cin(C8), .SUMout(SUM_out[9]), .Cout(C9));
  ALU_full_adder alu_full_adder_11 (.Xin(Ain[10]), .Yin(Bin[10]), .Cin(C9), .SUMout(SUM_out[10]), .Cout(C10));
  ALU_full_adder alu_full_adder_12 (.Xin(Ain[11]), .Yin(Bin[11]), .Cin(C10), .SUMout(SUM_out[11]), .Cout(C11));
  ALU_full_adder alu_full_adder_13 (.Xin(Ain[12]), .Yin(Bin[12]), .Cin(C11), .SUMout(SUM_out[12]), .Cout(C12));
  ALU_full_adder alu_full_adder_14 (.Xin(Ain[13]), .Yin(Bin[13]), .Cin(C12), .SUMout(SUM_out[13]), .Cout(C13));
  ALU_full_adder alu_full_adder_15 (.Xin(Ain[14]), .Yin(Bin[14]), .Cin(C13), .SUMout(SUM_out[14]), .Cout(C14));
  ALU_full_adder alu_full_adder_16 (.Xin(Ain[15]), .Yin(Bin[15]), .Cin(C14), .SUMout(SUM_out[15]), .Cout(Carry_out));

  // Other names for the same wires on the sheet: A0 = Ain[0]; A1 = Ain[1]; A2 = Ain[2]; A3 = Ain[3]; A4 = Ain[4];
  //   A5 = Ain[5]; A6 = Ain[6]; A7 = Ain[7]; A8 = Ain[8]; A9 = Ain[9]; A10 = Ain[10]; A11 = Ain[11]; A12 = Ain[12];
  //   A13 = Ain[13]; A14 = Ain[14]; A15 = Ain[15]; B0 = Bin[0]; B1 = Bin[1]; B2 = Bin[2]; B3 = Bin[3]; B4 = Bin[4];
  //   B5 = Bin[5]; B6 = Bin[6]; B7 = Bin[7]; B8 = Bin[8]; B9 = Bin[9]; B10 = Bin[10]; B11 = Bin[11]; B12 = Bin[12];
  //   B13 = Bin[13]; B14 = Bin[14]; B15 = Bin[15]; Cin = Carryin; Cout = Carry_out
endmodule

module main (
  input  [3:0] in_1,
  input  [15:0] in_2,
  input  [15:0] in_3,
  input  in_4,
  output [15:0] out_5,
  output out_6
);

  ALU alu_1 (.ALUC(in_1), .A(in_2), .B(in_3), .CYin(in_4), .Z(out_5), .CYout(out_6));
endmodule
