// Logisim project Bloque1.circ as structural Verilog: 1 circuit, main circuit Bloque1
module Bloque1 (
  input  [15:0] WRegister,
  input  CY,
  input  [1:0] B12B11,
  output Preload
);

  wire not_1_out, or_1_out;

  or or_1 (or_1_out, WRegister[0], WRegister[1], WRegister[2], WRegister[3], WRegister[4], WRegister[5], WRegister[6], WRegister[7], WRegister[8], WRegister[9], WRegister[10], WRegister[11], WRegister[12], WRegister[13], WRegister[14], WRegister[15]);
  not not_1 (not_1_out, or_1_out);
  Multiplexer #(.select(2), .enable("false")) multiplexer_1 (
    .in0(1'b1), .in1(not_1_out), .in2(WRegister[15]), .in3(CY), .out(Preload), .sel(B12B11));
endmodule
