// Logisim project UC1.circ as structural Verilog: 1 circuit, main circuit UC1
module UC1 (
  input  [31:0] Serial_IN,
  input  [9:0] DAddress_IN,
  output ALULatchEnable,
  output ALUEnable,
  output LoadStoreEnable,
  output LoadStoreLatchEnable
);

  wire [9:0] DAddress_ALU_IN, DAddress_Store_IN;
  wire [31:0] Serial_ALU_IN, Serial_Load_IN;

  or or_1 (LoadStoreEnable, Serial_IN[7], Serial_IN[8]);
  not not_1 (ALUEnable, LoadStoreEnable);
  Demultiplexer #(.width(32), .enable("false")) demultiplexer_1 (
    .out0(Serial_ALU_IN), .out1(Serial_Load_IN), .in(Serial_IN), .sel(LoadStoreEnable));
  Demultiplexer #(.width(10), .enable("false")) demultiplexer_2 (
    .out0(DAddress_ALU_IN), .out1(DAddress_Store_IN), .in(DAddress_IN), .sel(LoadStoreEnable));

  assign ALULatchEnable = ALUEnable;
  assign LoadStoreLatchEnable = LoadStoreEnable;
endmodule
